// Logisim project DED.circ as structural Verilog: 1 circuit, main circuit main
module main (
);

  wire clock_1_out, comparator_1_eq, comparator_2_eq, comparator_2_gt, or_1_out, or_2_out, Tens_carry,
       Units_carry;
  wire [11:0] Units_q;

  Clock clock_1 (.out(clock_1_out));
  Comparator #(.width(12)) comparator_1 (.a(Units_q), .b(12'h140), .eq(comparator_1_eq));  // open: gt, lt
  or or_1 (or_1_out, comparator_1_eq, clock_1_out);
  Counter #(.width(4), .max('h9)) Units (
    .Q(Units_q[3:0]), .carry(Units_carry), .clk(or_1_out));  // open: load, D, count, clr
  Counter #(.width(4), .max('h9), .trigger("falling")) Tens (
    .Q(Units_q[7:4]), .carry(Tens_carry), .clk(Units_carry));  // open: load, D, count, clr
  Counter #(.width(4), .max('h9), .trigger("falling")) Hundreds (
    .Q(Units_q[11:8]), .clk(Tens_carry));  // open: load, D, count, carry, clr
  Comparator #(.width(12)) comparator_2 (
    .a(Units_q), .b(12'h120), .gt(comparator_2_gt), .eq(comparator_2_eq));  // open: lt
  Hex_Digit_Display hex_digit_display_1 (.value(Units_q[11:8]));  // open: dp
  or or_2 (or_2_out, comparator_2_gt, comparator_2_eq);
  Hex_Digit_Display hex_digit_display_2 (.value(Units_q[7:4]));  // open: dp
  Hex_Digit_Display hex_digit_display_3 (.value(Units_q[3:0]));  // open: dp
  LED led_1 (.in(or_2_out));
endmodule
